# Fritzing sketch LcdProgressBarPot (saved by Fritzing 0.9.3b)
circuit board: 8.402cm x 5.73201cm
breadboards: 1

parts:
  LCD = LCD screen
  RTrimLCD = Trimmer Potentiometer [maximum_resistance=10kΩ package=THT]
  RLCD = Resistor [tolerance=±5% resistance=220 package=THT]
  UNO = Arduino Uno (Rev3)
  R5 = Trimmer Potentiometer [maximum_resistance=10kΩ package=THT]
  R4 = Trimmer Potentiometer [maximum_resistance=10kΩ package=THT]

nets:
  VSS: LCD.VSS, LCD.R/W, LCD.LED-, RTrimLCD.leg2, UNO.GND, R5.leg1, R4.leg1
  VDD: LCD.VDD, RTrimLCD.leg1, RLCD.Pin_1, UNO.5V, R5.leg2, R4.leg2
  N1: LCD.V0, RTrimLCD.wiper
  N2: LCD.RS, UNO.D12/MISO
  N3: LCD.E, UNO.D11_PWM/MOSI
  N4: LCD.DB4, UNO.D5_PWM
  N5: LCD.DB5, UNO.D4
  N6: LCD.DB6, UNO.D3_PWM
  N7: LCD.DB7, UNO.D2
  N8: LCD.LED+, RLCD.Pin_0
  N9: UNO.A4/SDA, R4.wiper
  N10: UNO.A5/SCL, R5.wiper
